// Logisim project UAL.circ as structural Verilog: 11 circuits, main circuit main
module main (
);

  wire button_1_out, clock_1_out, decodeur_instructions_1_isjmp, decodeur_instructions_1_isload,
       decodeur_instructions_1_regwrite;
  wire [1:0] ctrl_saut_1_nextpcselect;
  wire [2:0] decodeur_instructions_1_ctrlual;
  wire [3:0] selection_registre_1_rd_res, selection_registre_1_rs_res, selection_registre_1_rt_res,
       ual_1_flags;
  wire [7:0] adder_1_out, adder_2_out, banc_registre_1_rs_2, banc_registre_1_rt_2, bit_extender_1_out,
       multiplexer_1_out, multiplexer_2_out, PC_q, ual_1_out_4;
  wire [15:0] ram_1_data;

  Button button_1 (.out(button_1_out));
  Register PC (.D(multiplexer_2_out), .en(button_1_out), .Q(PC_q), .clk(clock_1_out));  // open: clr
  Clock clock_1 (.out(clock_1_out));
  RAM #(.dataWidth(16)) ram_1 (.addr(PC_q), .data(ram_1_data), .clk(clock_1_out));  // open: sel, ld, clr
  Decodeur_Instructions decodeur_instructions_1 (
    .isJMP(decodeur_instructions_1_isjmp), .regWrite(decodeur_instructions_1_regwrite),
    .isLoad(decodeur_instructions_1_isload), .ctrlUAL(decodeur_instructions_1_ctrlual),
    .opcode(ram_1_data[15:12]));
  Selection_Registre selection_registre_1 (
    .rd(ram_1_data[11:8]), .rs(ram_1_data[7:4]), .rt(ram_1_data[3:0]), .isJMP(decodeur_instructions_1_isjmp),
    .rd_res(selection_registre_1_rd_res), .rs_res(selection_registre_1_rs_res),
    .rt_res(selection_registre_1_rt_res));
  Adder adder_1 (.a(PC_q), .b(8'h1), .out(adder_1_out));  // open: cin, cout
  Banc_Registre banc_registre_1 (
    .RESET(button_1_out), .regWrite(decodeur_instructions_1_regwrite), .RT_2(banc_registre_1_rt_2),
    .valIn(multiplexer_1_out), .RS_2(banc_registre_1_rs_2), .rd(selection_registre_1_rd_res),
    .rt(selection_registre_1_rt_res), .rs(selection_registre_1_rs_res));
  Multiplexer #(.width(8)) multiplexer_1 (
    .in0(ram_1_data[7:0]), .in1(ual_1_out_4), .out(multiplexer_1_out), .sel(decodeur_instructions_1_isload));  // open: en
  assign bit_extender_1_out = {{4{1'b0}}, ram_1_data[3:0]};  // Bit_Extender bit_extender_1
  UAL ual_1 (
    .in_1(decodeur_instructions_1_ctrlual), .in_2(banc_registre_1_rs_2), .in_3(banc_registre_1_rt_2),
    .out_4(ual_1_out_4), .Flags(ual_1_flags));
  Adder adder_2 (.a(adder_1_out), .b(bit_extender_1_out), .out(adder_2_out));  // open: cin, cout
  Multiplexer #(.select(2), .width(8)) multiplexer_2 (
    .in0(adder_1_out), .in1({8{1'b1}}), .in2(adder_2_out), .out(multiplexer_2_out),
    .sel(ctrl_saut_1_nextpcselect));  // open: in3, en
  Ctrl_Saut ctrl_saut_1 (.flags(ual_1_flags), .nextPCselect(ctrl_saut_1_nextpcselect), .opcode(ram_1_data[15:12]));

  // Notes on the sheet:
  //   {Reset}
  //   isJMP
  //   regWrite
  //   valIn
  //   isLoad
  //   "HALT"
  //   Rs
  //   Rt
  //   "instruction suivante"
  //   ctrlUAL
  //   "saut"
  //   nextPCselect
endmodule

module Decodeur_Instructions (
  input  [3:0] opcode,
  output isJMP,
  output regWrite,
  output isLoad,
  output [2:0] ctrlUAL
);

  wire add, \and , b, beq, bge, bgt, ble, blt, bne, halt, \not , Or, shl, shr, sub;

  Demultiplexer #(.select(4)) demultiplexer_1 (
    .out0(add), .out1(sub), .out2(Or), .out3(\and ), .out4(\not ), .out5(shl), .out6(shr), .out7(isLoad),
    .out8(halt), .out9(b), .out10(beq), .out11(bne), .out12(bge), .out13(ble), .out14(bgt), .out15(blt),
    .in(1'b1), .sel(opcode));  // open: en
  Multiplexer #(.select(4), .width(3)) multiplexer_1 (
    .in0(3'b000), .in1(3'b001), .in2(3'b010), .in3(3'b011), .in4(3'b100), .in5(3'b101), .in6(3'b110),
    .in7(3'b111), .in8(3'b111), .in9(3'b111), .in10(3'b001), .in11(3'b001), .in12(3'b001), .in13(3'b001),
    .in14(3'b001), .in15(3'b001), .out(ctrlUAL), .sel(opcode));  // open: en
  or or_1 (isJMP, b, beq, bne, bge, ble, bgt, blt);
  or or_2 (regWrite, add, sub, Or, \and , \not , shl, shr);

  // Other names for the same wires on the sheet: li = isLoad
endmodule

module UAL (
  input  [2:0] in_1,
  input  [7:0] in_2,
  input  [7:0] in_3,
  output [7:0] out_4,
  output [3:0] Flags
);

  wire and_2_out, and_3_out, and_5_out, and_6_out, CF_minus, CF_plus, OF_minus, OF_plus;
  wire [7:0] AND, l, NOT, OR, r, tunnel, tunnel_t;

  Multiplexer #(.select(3)) multiplexer_1 (
    .in0(CF_plus), .in1(CF_minus), .in2(1'b0), .in3(1'b0), .in4(1'b0), .in5(1'b0), .in6(1'b0), .in7(1'b0),
    .out(Flags[3]), .sel(in_1));  // open: en
  assign NOT = ~in_2;  // NOT_Gate not_1, 8 bits wide
  Adder adder_1 (.a(in_2), .b(in_3), .out(tunnel), .cout(CF_plus));  // open: cin
  Subtractor subtractor_1 (.a(in_2), .b(in_3), .out(tunnel_t), .bout(CF_minus));  // open: bin
  assign OR = in_2 | in_3;  // OR_Gate or_1, 8 bits wide
  assign AND = in_2 & in_3;  // AND_Gate and_1, 8 bits wide
  Shifter shifter_1 (.in(in_2), .\dist (in_3[2:0]), .out(l));
  Shifter #(.shift("lr")) shifter_2 (.in(in_2), .\dist (in_3[2:0]), .out(r));
  and and_2 (and_2_out, in_2[7], in_3[7], ~Flags[1]);  // AND_Gate
  and and_3 (and_3_out, ~in_2[7], ~in_3[7], Flags[1]);  // AND_Gate
  or or_2 (OF_plus, and_2_out, and_3_out);
  Multiplexer #(.select(3), .width(8)) multiplexer_2 (
    .in0(tunnel), .in1(tunnel_t), .in2(OR), .in3(AND), .in4(NOT), .in5(l), .in6(r), .in7({8{1'b0}}),
    .out({Flags[1], out_4[6:0]}), .sel(in_1));  // open: en
  and and_4 (Flags[2], ~Flags[1], ~out_4[6], ~out_4[5], ~out_4[4], ~out_4[3], ~out_4[2], ~out_4[1], ~out_4[0]);  // AND_Gate
  and and_5 (and_5_out, in_2[7], ~in_3[7], ~Flags[1]);  // AND_Gate
  or or_3 (OF_minus, and_5_out, and_6_out);
  and and_6 (and_6_out, ~in_2[7], in_3[7], Flags[1]);  // AND_Gate
  Multiplexer #(.select(3), .enable("false")) multiplexer_3 (
    .in0(OF_plus), .in1(OF_minus), .in2(1'b0), .in3(1'b0), .in4(1'b0), .in5(1'b0), .in6(1'b0), .in7(1'b0),
    .out(Flags[0]), .sel(in_1));

  assign out_4[7] = Flags[1];

  // Other names for the same wires on the sheet: ctrlUAL[2:0] = in_1; OF = Flags[0]; OFres = Flags[1]; SF = Flags[1];
  //   ZF = Flags[2]; CF = Flags[3]; rs[7:0] = in_2; OFrs = in_2[7]; rt[7:0] = in_3; OFrt = in_3[7]

  // Notes on the sheet:
  //   Carry Flag
  //   Opérations
  //   Overflow Flag
  //   Sélection
  //   Sign Flag
  //   Zero Flag
  //   Mémo
  //   000 : addition
  //   001 : soustraction
  //   010 : OU bit-à-bit
  //   011 : ET bit-à-bit
  //   100 : NON bit-à-bit
  //   101 : décalage gauche
  //   110 : décalage droite
  //   111 : ???
  //   Flags
endmodule

module Ctrl_Saut (
  input  [3:0] opcode,
  input  [3:0] flags,
  output [1:0] nextPCselect
);

  wire and_1_out, and_2_out, and_3_out, and_4_out, and_5_out, and_6_out, and_7_out, and_8_out;
  wire [1:1] bge, bgt, ble, blt, bne;

  not not_1 (bne[1], flags[2]);
  and and_1 (and_1_out, flags[1], flags[0]);
  and and_2 (and_2_out, ~flags[1], ~flags[0]);  // AND_Gate
  and and_3 (and_3_out, ~flags[1], flags[0]);  // AND_Gate
  and and_4 (and_4_out, flags[1], ~flags[0]);  // AND_Gate
  and and_5 (and_5_out, ~flags[2], ~flags[1], ~flags[0]);  // AND_Gate
  and and_6 (and_6_out, ~flags[2], flags[1], flags[0]);  // AND_Gate
  and and_7 (and_7_out, flags[1], ~flags[0]);  // AND_Gate
  and and_8 (and_8_out, ~flags[1], flags[0]);  // AND_Gate
  or or_1 (bge[1], and_1_out, and_2_out);
  or or_2 (ble[1], and_3_out, flags[2], and_4_out);
  or or_3 (bgt[1], and_5_out, and_6_out);
  or or_4 (blt[1], and_7_out, and_8_out);
  Multiplexer #(.select(4), .width(2)) multiplexer_1 (
    .in0(2'b00), .in1(2'b00), .in2(2'b00), .in3(2'b00), .in4(2'b00), .in5(2'b00), .in6(2'b00), .in7(2'b00),
    .in8(2'b01), .in9(2'b10), .in10({flags[2], 1'b0}), .in11({bne[1], 1'b0}), .in12({bge[1], 1'b0}),
    .in13({ble[1], 1'b0}), .in14({bgt[1], 1'b0}), .in15({blt[1], 1'b0}), .out(nextPCselect), .sel(opcode));  // open: en

  // Other names for the same wires on the sheet: OF = flags[0]; SF = flags[1]; beq[1] = flags[2]; ZF = flags[2];
  //   CF = flags[3]

  // Notes on the sheet:
  //   beq
  //   bne
  //   bge
  //   ble
  //   bgt
  //   blt
endmodule

module Banc_Registre (
  input  RESET,
  input  regWrite,
  input  [7:0] valIn,
  input  [3:0] rt,
  input  [3:0] rs,
  input  [3:0] rd,
  output [7:0] RT_2,
  output [7:0] RS_2
);

  wire clock;
  wire [7:0] _1res, _2res, _3res, _4res, _5res, _6res, _7res, _8res, _9res, _10res, _11res, _12res, _13res,
       _14res, _15res, _16res, demultiplexer_1_out0, demultiplexer_1_out1, demultiplexer_1_out2,
       demultiplexer_1_out3, demultiplexer_1_out4, demultiplexer_1_out5, demultiplexer_1_out6,
       demultiplexer_1_out7, demultiplexer_1_out8, demultiplexer_1_out9, demultiplexer_1_out10,
       demultiplexer_1_out11, demultiplexer_1_out12, demultiplexer_1_out13, demultiplexer_1_out14,
       demultiplexer_1_out15, reg1, reg2, reg3, reg4, reg5, reg6, reg7, reg8, reg9, reg10, reg11, reg12,
       reg13, reg14, reg15, reg16;

  Clock u_clock (.out(clock));
  Register register_1 (.D(reg1), .Q(_1res), .clk(clock), .clr(RESET));  // open: en
  Register register_2 (.D(reg9), .Q(_9res), .clk(clock), .clr(RESET));  // open: en
  Demultiplexer #(.select(4), .width(8)) demultiplexer_1 (
    .out0(demultiplexer_1_out0), .out1(demultiplexer_1_out1), .out2(demultiplexer_1_out2),
    .out3(demultiplexer_1_out3), .out4(demultiplexer_1_out4), .out5(demultiplexer_1_out5),
    .out6(demultiplexer_1_out6), .out7(demultiplexer_1_out7), .out8(demultiplexer_1_out8),
    .out9(demultiplexer_1_out9), .out10(demultiplexer_1_out10), .out11(demultiplexer_1_out11),
    .out12(demultiplexer_1_out12), .out13(demultiplexer_1_out13), .out14(demultiplexer_1_out14),
    .out15(demultiplexer_1_out15), .in(valIn), .sel(rd));  // open: en
  Register register_3 (.D(reg2), .Q(_2res), .clk(clock), .clr(RESET));  // open: en
  Register register_4 (.D(reg10), .Q(_10res), .clk(clock), .clr(RESET));  // open: en
  Transistor #(.\type ("n"), .width(8)) transistor_1 (.in(demultiplexer_1_out0), .out(reg1), .gate(regWrite));
  Transistor #(.\type ("n"), .width(8)) transistor_2 (.in(demultiplexer_1_out1), .out(reg2), .gate(regWrite));
  Transistor #(.\type ("n"), .gate("br"), .width(8)) transistor_3 (
    .in(demultiplexer_1_out14), .out(reg15), .gate(regWrite));
  Transistor #(.\type ("n"), .gate("br"), .width(8)) transistor_4 (
    .in(demultiplexer_1_out15), .out(reg16), .gate(regWrite));
  Register register_5 (.D(reg3), .Q(_3res), .clk(clock), .clr(RESET));  // open: en
  Register register_6 (.D(reg11), .Q(_11res), .clk(clock), .clr(RESET));  // open: en
  Transistor #(.\type ("n"), .width(8)) transistor_5 (.in(demultiplexer_1_out2), .out(reg3), .gate(regWrite));
  Transistor #(.\type ("n"), .width(8)) transistor_6 (.in(demultiplexer_1_out3), .out(reg4), .gate(regWrite));
  Transistor #(.\type ("n"), .gate("br"), .width(8)) transistor_7 (
    .in(demultiplexer_1_out12), .out(reg13), .gate(regWrite));
  Transistor #(.\type ("n"), .gate("br"), .width(8)) transistor_8 (
    .in(demultiplexer_1_out13), .out(reg14), .gate(regWrite));
  Transistor #(.\type ("n"), .width(8)) transistor_9 (.in(demultiplexer_1_out4), .out(reg5), .gate(regWrite));
  Transistor #(.\type ("n"), .width(8)) transistor_10 (.in(demultiplexer_1_out5), .out(reg6), .gate(regWrite));
  Transistor #(.\type ("n"), .width(8)) transistor_11 (.in(demultiplexer_1_out6), .out(reg7), .gate(regWrite));
  Transistor #(.\type ("n"), .gate("br"), .width(8)) transistor_12 (
    .in(demultiplexer_1_out9), .out(reg10), .gate(regWrite));
  Transistor #(.\type ("n"), .gate("br"), .width(8)) transistor_13 (
    .in(demultiplexer_1_out10), .out(reg11), .gate(regWrite));
  Transistor #(.\type ("n"), .gate("br"), .width(8)) transistor_14 (
    .in(demultiplexer_1_out11), .out(reg12), .gate(regWrite));
  Register register_7 (.D(reg4), .Q(_4res), .clk(clock), .clr(RESET));  // open: en
  Register register_8 (.D(reg12), .Q(_12res), .clk(clock), .clr(RESET));  // open: en
  Transistor #(.\type ("n"), .width(8)) transistor_15 (.in(demultiplexer_1_out7), .out(reg8), .gate(regWrite));
  Transistor #(.\type ("n"), .gate("br"), .width(8)) transistor_16 (
    .in(demultiplexer_1_out8), .out(reg9), .gate(regWrite));
  Register register_9 (.D(reg5), .Q(_5res), .clk(clock), .clr(RESET));  // open: en
  Register register_10 (.D(reg13), .Q(_13res), .clk(clock), .clr(RESET));  // open: en
  Multiplexer #(.select(4), .width(8)) multiplexer_1 (
    .in0(_1res), .in1(_2res), .in2(_3res), .in3(_4res), .in4(_5res), .in5(_6res), .in6(_7res), .in7(_8res),
    .in8(_9res), .in9(_10res), .in10(_11res), .in11(_12res), .in12(_13res), .in13(_14res), .in14(_15res),
    .in15(_16res), .out(RT_2), .sel(rt));  // open: en
  Register register_11 (.D(reg6), .Q(_6res), .clk(clock), .clr(RESET));  // open: en
  Register register_12 (.D(reg14), .Q(_14res), .clk(clock), .clr(RESET));  // open: en
  Register register_13 (.D(reg7), .Q(_7res), .clk(clock), .clr(RESET));  // open: en
  Register register_14 (.D(reg15), .Q(_15res), .clk(clock), .clr(RESET));  // open: en
  Multiplexer #(.select(4), .width(8)) multiplexer_2 (
    .in0(_1res), .in1(_2res), .in2(_3res), .in3(_4res), .in4(_5res), .in5(_6res), .in6(_7res), .in7(_8res),
    .in8(_9res), .in9(_10res), .in10(_11res), .in11(_12res), .in12(_13res), .in13(_14res), .in14(_15res),
    .in15(_16res), .out(RS_2), .sel(rs));  // open: en
  Register register_15 (.D(reg8), .Q(_8res), .clk(clock), .clr(RESET));  // open: en
  Register register_16 (.D(reg16), .Q(_16res), .clk(clock), .clr(RESET));  // open: en
endmodule

module Selection_Registre (
  input  [3:0] rd,
  input  [3:0] rs,
  input  [3:0] rt,
  input  isJMP,
  output [3:0] rd_res,
  output [3:0] rs_res,
  output [3:0] rt_res
);

  Multiplexer #(.width(4)) multiplexer_1 (.in0(rd), .in1(rs), .out(rd_res), .sel(isJMP));  // open: en
  Multiplexer #(.width(4)) multiplexer_2 (.in0(rs), .in1(rt), .out(rs_res), .sel(isJMP));  // open: en

  assign rt_res = rt;

  // Other names for the same wires on the sheet: jump = isJMP
endmodule

module Test_UAL (
  input  [7:0] Rs,
  input  [7:0] Rt,
  input  [2:0] in_3,
  output [3:0] C_Z_S_O_flags,
  output [7:0] \résultat 
);

  UAL ual_1 (.in_1(in_3), .in_2(Rs), .in_3(Rt), .out_4(\résultat ), .Flags(C_Z_S_O_flags));
endmodule

module Test_Ctrl_Saut (
  input  [3:0] C_Z_S_O_flags,
  input  [3:0] opcode,
  output [1:0] nextPCselect
);

  Ctrl_Saut ctrl_saut_1 (.flags(C_Z_S_O_flags), .nextPCselect(nextPCselect), .opcode(opcode));
endmodule

module Test_Banc_Registre (
  input  [3:0] rd,
  input  [3:0] rs,
  input  [3:0] rt,
  input  regWrite,
  input  [7:0] valIn,
  output [7:0] Rs_2,
  output [7:0] Rt_2
);

  wire Reset_out;

  Button Reset (.out(Reset_out));
  Banc_Registre banc_registre_1 (
    .RESET(Reset_out), .regWrite(regWrite), .RT_2(Rt_2), .valIn(valIn), .RS_2(Rs_2), .rd(rd), .rt(rt), .rs(rs));
endmodule

module Test_Decodeur_Instruction (
  input  [3:0] opcode,
  output isJMP,
  output regWrite,
  output isLoad,
  output [2:0] ctrlUAL
);

  Decodeur_Instructions decodeur_instructions_1 (
    .isJMP(isJMP), .regWrite(regWrite), .isLoad(isLoad), .ctrlUAL(ctrlUAL), .opcode(opcode));
endmodule

module Test_Selection_Registre (
  input  [3:0] rd,
  input  [3:0] rs,
  input  [3:0] rt,
  input  isJMP,
  output [3:0] rd_res,
  output [3:0] rs_res,
  output [3:0] rt_res
);

  Selection_Registre selection_registre_1 (
    .rd(rd), .rs(rs), .rt(rt), .isJMP(isJMP), .rd_res(rd_res), .rs_res(rs_res), .rt_res(rt_res));
endmodule
