// Logisim project ctrl saut.circ as structural Verilog: 3 circuits, main circuit main
module main (
  input  [3:0] opcode,
  input  [3:0] flags,
  output [1:0] nextPCselect
);

  wire and_1_out, and_2_out, and_3_out, and_4_out, and_5_out, and_6_out, and_7_out, and_8_out;
  wire [1:1] bge, bgt, ble, blt, bne;

  not not_1 (bne[1], flags[2]);
  and and_1 (and_1_out, flags[1], flags[0]);
  and and_2 (and_2_out, ~flags[1], ~flags[0]);  // AND_Gate
  and and_3 (and_3_out, ~flags[1], flags[0]);  // AND_Gate
  and and_4 (and_4_out, flags[1], ~flags[0]);  // AND_Gate
  and and_5 (and_5_out, ~flags[2], ~flags[1], ~flags[0]);  // AND_Gate
  and and_6 (and_6_out, ~flags[2], flags[1], flags[0]);  // AND_Gate
  and and_7 (and_7_out, flags[1], ~flags[0]);  // AND_Gate
  and and_8 (and_8_out, ~flags[1], flags[0]);  // AND_Gate
  or or_1 (bge[1], and_1_out, and_2_out);
  or or_2 (ble[1], and_3_out, flags[2], and_4_out);
  or or_3 (bgt[1], and_5_out, and_6_out);
  or or_4 (blt[1], and_7_out, and_8_out);
  Multiplexer #(.select(4), .width(2)) multiplexer_1 (
    .in0(2'b00), .in1(2'b00), .in2(2'b00), .in3(2'b00), .in4(2'b00), .in5(2'b00), .in6(2'b00), .in7(2'b00),
    .in8(2'b01), .in9(2'b10), .in10({flags[2], 1'b0}), .in11({bne[1], 1'b0}), .in12({bge[1], 1'b0}),
    .in13({ble[1], 1'b0}), .in14({bgt[1], 1'b0}), .in15({blt[1], 1'b0}), .out(nextPCselect), .sel(opcode));  // open: en

  // Other names for the same wires on the sheet: OF = flags[0]; SF = flags[1]; beq[1] = flags[2]; ZF = flags[2];
  //   CF = flags[3]

  // Notes on the sheet:
  //   beq
  //   bne
  //   bge
  //   ble
  //   bgt
  //   blt
endmodule

module banc (
  input  RESET,
  input  regWrite,
  input  [7:0] valIn,
  input  [3:0] rt,
  input  [3:0] rs,
  input  [3:0] rd,
  output [7:0] RT_2,
  output [7:0] RS_2
);

  wire clock;
  wire [7:0] _1res, _2res, _3res, _4res, _5res, _6res, _7res, _8res, _9res, _10res, _11res, _12res, _13res,
       _14res, _15res, _16res, demultiplexer_1_out0, demultiplexer_1_out1, demultiplexer_1_out2,
       demultiplexer_1_out3, demultiplexer_1_out4, demultiplexer_1_out5, demultiplexer_1_out6,
       demultiplexer_1_out7, demultiplexer_1_out8, demultiplexer_1_out9, demultiplexer_1_out10,
       demultiplexer_1_out11, demultiplexer_1_out12, demultiplexer_1_out13, demultiplexer_1_out14,
       demultiplexer_1_out15, reg1, reg2, reg3, reg4, reg5, reg6, reg7, reg8, reg9, reg10, reg11, reg12,
       reg13, reg14, reg15, reg16;

  Clock clock_1 (.out(clock));
  Register register_1 (.D(reg1), .Q(_1res), .clk(clock), .clr(RESET));  // open: en
  Register register_2 (.D(reg9), .Q(_9res), .clk(clock), .clr(RESET));  // open: en
  Demultiplexer #(.select(4), .width(8)) demultiplexer_1 (
    .out0(demultiplexer_1_out0), .out1(demultiplexer_1_out1), .out2(demultiplexer_1_out2),
    .out3(demultiplexer_1_out3), .out4(demultiplexer_1_out4), .out5(demultiplexer_1_out5),
    .out6(demultiplexer_1_out6), .out7(demultiplexer_1_out7), .out8(demultiplexer_1_out8),
    .out9(demultiplexer_1_out9), .out10(demultiplexer_1_out10), .out11(demultiplexer_1_out11),
    .out12(demultiplexer_1_out12), .out13(demultiplexer_1_out13), .out14(demultiplexer_1_out14),
    .out15(demultiplexer_1_out15), .in(valIn), .sel(rd));  // open: en
  Register register_3 (.D(reg2), .Q(_2res), .clk(clock), .clr(RESET));  // open: en
  Register register_4 (.D(reg10), .Q(_10res), .clk(clock), .clr(RESET));  // open: en
  Transistor #(.\type ("n"), .width(8)) transistor_1 (.in(demultiplexer_1_out0), .out(reg1), .gate(regWrite));
  Transistor #(.\type ("n"), .width(8)) transistor_2 (.in(demultiplexer_1_out1), .out(reg2), .gate(regWrite));
  Transistor #(.\type ("n"), .gate("br"), .width(8)) transistor_3 (
    .in(demultiplexer_1_out14), .out(reg15), .gate(regWrite));
  Transistor #(.\type ("n"), .gate("br"), .width(8)) transistor_4 (
    .in(demultiplexer_1_out15), .out(reg16), .gate(regWrite));
  Register register_5 (.D(reg3), .Q(_3res), .clk(clock), .clr(RESET));  // open: en
  Register register_6 (.D(reg11), .Q(_11res), .clk(clock), .clr(RESET));  // open: en
  Transistor #(.\type ("n"), .width(8)) transistor_5 (.in(demultiplexer_1_out2), .out(reg3), .gate(regWrite));
  Transistor #(.\type ("n"), .width(8)) transistor_6 (.in(demultiplexer_1_out3), .out(reg4), .gate(regWrite));
  Transistor #(.\type ("n"), .gate("br"), .width(8)) transistor_7 (
    .in(demultiplexer_1_out12), .out(reg13), .gate(regWrite));
  Transistor #(.\type ("n"), .gate("br"), .width(8)) transistor_8 (
    .in(demultiplexer_1_out13), .out(reg14), .gate(regWrite));
  Transistor #(.\type ("n"), .width(8)) transistor_9 (.in(demultiplexer_1_out4), .out(reg5), .gate(regWrite));
  Transistor #(.\type ("n"), .width(8)) transistor_10 (.in(demultiplexer_1_out5), .out(reg6), .gate(regWrite));
  Transistor #(.\type ("n"), .width(8)) transistor_11 (.in(demultiplexer_1_out6), .out(reg7), .gate(regWrite));
  Transistor #(.\type ("n"), .gate("br"), .width(8)) transistor_12 (
    .in(demultiplexer_1_out9), .out(reg10), .gate(regWrite));
  Transistor #(.\type ("n"), .gate("br"), .width(8)) transistor_13 (
    .in(demultiplexer_1_out10), .out(reg11), .gate(regWrite));
  Transistor #(.\type ("n"), .gate("br"), .width(8)) transistor_14 (
    .in(demultiplexer_1_out11), .out(reg12), .gate(regWrite));
  Register register_7 (.D(reg4), .Q(_4res), .clk(clock), .clr(RESET));  // open: en
  Register register_8 (.D(reg12), .Q(_12res), .clk(clock), .clr(RESET));  // open: en
  Transistor #(.\type ("n"), .width(8)) transistor_15 (.in(demultiplexer_1_out7), .out(reg8), .gate(regWrite));
  Transistor #(.\type ("n"), .gate("br"), .width(8)) transistor_16 (
    .in(demultiplexer_1_out8), .out(reg9), .gate(regWrite));
  Register register_9 (.D(reg5), .Q(_5res), .clk(clock), .clr(RESET));  // open: en
  Register register_10 (.D(reg13), .Q(_13res), .clk(clock), .clr(RESET));  // open: en
  Multiplexer #(.select(4), .width(8)) multiplexer_1 (
    .in0(_1res), .in1(_2res), .in2(_3res), .in3(_4res), .in4(_5res), .in5(_6res), .in6(_7res), .in7(_8res),
    .in8(_9res), .in9(_10res), .in10(_11res), .in11(_12res), .in12(_13res), .in13(_14res), .in14(_15res),
    .in15(_16res), .out(RT_2), .sel(rt));  // open: en
  Register register_11 (.D(reg6), .Q(_6res), .clk(clock), .clr(RESET));  // open: en
  Register register_12 (.D(reg14), .Q(_14res), .clk(clock), .clr(RESET));  // open: en
  Register register_13 (.D(reg7), .Q(_7res), .clk(clock), .clr(RESET));  // open: en
  Register register_14 (.D(reg15), .Q(_15res), .clk(clock), .clr(RESET));  // open: en
  Multiplexer #(.select(4), .width(8)) multiplexer_2 (
    .in0(_1res), .in1(_2res), .in2(_3res), .in3(_4res), .in4(_5res), .in5(_6res), .in6(_7res), .in7(_8res),
    .in8(_9res), .in9(_10res), .in10(_11res), .in11(_12res), .in12(_13res), .in13(_14res), .in14(_15res),
    .in15(_16res), .out(RS_2), .sel(rs));  // open: en
  Register register_15 (.D(reg8), .Q(_8res), .clk(clock), .clr(RESET));  // open: en
  Register register_16 (.D(reg16), .Q(_16res), .clk(clock), .clr(RESET));  // open: en
endmodule

module select_reg (
  input  [3:0] rd,
  input  [3:0] rs,
  input  [3:0] rt,
  input  isJMP,
  output [3:0] rd_res,
  output [3:0] rs_res,
  output [3:0] rt_res
);

  Multiplexer #(.width(4)) multiplexer_1 (.in0(rd), .in1(rs), .out(rd_res), .sel(isJMP));  // open: en
  Multiplexer #(.width(4)) multiplexer_2 (.in0(rs), .in1(rt), .out(rs_res), .sel(isJMP));  // open: en

  assign rt_res = rt;

  // Other names for the same wires on the sheet: jump = isJMP
endmodule
